# Fritzing sketch spirometer circuit (saved by Fritzing 0.9.10b)
circuit board: 8.46667cm x 5.64444cm
breadboards: 1

parts:
  MCU1 = Raspberry Pi Zero
  U1 = LCD-16X2 [package=lcd-16x2_noholes]
  Q1 = PHOTOTRANSISTOR REFLECTIVE OBJECT SENSOR [package=qrb1114-side]
  R1 = PHOTOCELL [package=photocell-kit]
  R2 = PHOTOCELL [package=photocell-kit]
  R3 = PHOTOCELL [package=photocell-kit]
  R4 = PHOTOCELL [package=photocell-kit]
  MPX4250AP1 = MPX4250AP pressure sensor [part_number=MPX]
  R6 = Resistor [tolerance=±5% power=0.25 resistance=2.2 package=THT]
  R7 = Resistor [tolerance=±5% resistance=1.5 package="0603 [SMD]"]
  BAT1 = Battery Holders [package=lipo-1100mAh]

nets:
  N1: MCU1.pin_1, MCU1.pin_17, U1.VSS, Q1.A, Q1.C, R1.P$1, R2.P$1, R3.P$1, R4.P$1, MPX4250AP1.Vs, BAT1.+
  N2: MCU1.pin_2, MCU1.pin_4, U1.VDD, U1.A
  N3: MCU1.pin_3, MPX4250AP1.V_out
  N4: MCU1.pin_6, MCU1.pin_7, MCU1.pin_9, MCU1.pin_14, MCU1.pin_20, MCU1.pin_25, MCU1.pin_30, MCU1.pin_34, MCU1.pin_39, U1.VO, U1.R_W, U1.K, R1.P$2, R2.P$2, R3.P$2, R4.P$2, MPX4250AP1.GND, R6.Pin_1, R7.Pin_1, BAT1.-
  N5: MCU1.pin_18, Q1.E, R6.Pin_0
  N6: MCU1.pin_23, U1.DB7
  N7: MCU1.pin_29, U1.DB6
  N8: MCU1.pin_31, U1.DB5
  N9: MCU1.pin_33, U1.DB4
  N10: MCU1.pin_35, U1.E
  N11: MCU1.pin_37, U1.RS
  N12: Q1.K, R7.Pin_0

// code stored in the sketch: spirometry.ino

