# Fritzing sketch spirometer (saved by Fritzing 0.9.10b)
breadboards: 1

parts:
  Part1 = Adafruit VL530X Time of Flight Distance Sensor [part_number="Adafruit #3317"]
  U1 = LCD-16X2 [package=lcd-16x2_noholes]
  Part2 = Arduino Uno (Rev3)
  U2 = POT [knob_status=50% power=0.5W package=pot_alpha_rv16af-20]

nets:
  GND: Part1.GND, U1.VSS, U1.R_W, Part2.GND, U2.E
  VCC: Part1.VCC, U1.VDD, Part2.5V, U2.A
  N1: Part1.SDA, Part2.A4/SDA
  N2: Part1.SCL, Part2.A5/SCL
  N3: U1.VO, U2.S
  N4: U1.RS, Part2.D10_PWM/SS
  N5: U1.E, Part2.D9_PWM
  N6: U1.DB4, Part2.D5_PWM
  N7: U1.DB5, Part2.D4
  N8: U1.DB6, Part2.D3_PWM
  N9: U1.DB7, Part2.D2

custom parts:
  Adafruit VL530X Time of Flight Distance Sensor: The VL53L0X is a Time of Flight distance sensor like no other you've used! The sensor contains a very tiny invisible laser source, and a matching sensor. The VL53L0X can detect the "time of flight", or how long the light has taken to bounce back to the sensor. Since it uses a very narrow light source, it is good for determining distance of only the surface directly in front of it. Unlike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
